// Logisim project hw3.circ as structural Verilog: 5 circuits, main circuit SR_Latch
module SR_Latch (
  input  in_1,
  input  in_2,
  output out_3,
  output out_4
);

  wire or_1_out, or_2_out;

  or or_1 (or_1_out, in_1, out_4);
  or or_2 (or_2_out, out_3, in_2);
  not not_1 (out_3, or_1_out);
  not not_2 (out_4, or_2_out);

  // Notes on the sheet:
  //   Provided for you
endmodule

module D_Latch (
  input  in_1,
  input  in_2,
  output out_3
);

  wire and_1_out, and_2_out, not_1_out;

  not not_1 (not_1_out, in_1);
  and and_1 (and_1_out, in_1, in_2);
  and and_2 (and_2_out, not_1_out, in_2);
  SR_Latch SR (.in_1(and_1_out), .in_2(and_2_out), .out_4(out_3));  // open: out_3

  // Notes on the sheet:
  //   Strobe
  //   Provided for you
  //   We ignore the NOT Q output
endmodule

module Decoder (
  input  in_1,
  input  in_2,
  output out_3,
  output out_4,
  output out_5,
  output out_6
);

  wire not_1_out, not_2_out, not_3_out, not_4_out;

  not not_1 (not_1_out, in_1);
  not not_2 (not_2_out, in_2);
  not not_3 (not_3_out, in_1);
  not not_4 (not_4_out, in_2);
  and and_1 (out_3, not_1_out, not_2_out);
  and and_2 (out_4, not_3_out, in_2);
  and and_3 (out_5, in_1, not_4_out);
  and and_4 (out_6, in_1, in_2);

  // Notes on the sheet:
  //   Provided for you
endmodule

module RAM (
  input  in_1,
  input  _2Bit_Addr,
  input  in_3,
  input  _3Bit_Data,
  input  in_5,
  input  Write,
  output out_7,
  output _3_Bit_Out,
  output out_9
);

  wire and_1_out, and_2_out, and_3_out, and_4_out, and_5_out, and_6_out, and_7_out, and_8_out, and_9_out,
       and_10_out, and_11_out, and_12_out, and_13_out, and_14_out, and_15_out, and_16_out, and_17_out,
       and_18_out, and_19_out, and_20_out, d_latch_1_out_3, d_latch_2_out_3, d_latch_3_out_3,
       d_latch_4_out_3, d_latch_5_out_3, d_latch_6_out_3, d_latch_7_out_3, d_latch_8_out_3, d_latch_9_out_3,
       d_latch_10_out_3, d_latch_11_out_3, d_latch_12_out_3, decoder_1_out_3, decoder_1_out_4,
       decoder_1_out_5, decoder_1_out_6, not_1_out;

  Decoder decoder_1 (
    .out_6(decoder_1_out_6), .out_3(decoder_1_out_3), .out_5(decoder_1_out_5), .out_4(decoder_1_out_4),
    .in_2(_2Bit_Addr), .in_1(in_1));
  not not_1 (not_1_out, Write);
  and and_1 (and_1_out, decoder_1_out_3, Write);
  and and_2 (and_2_out, decoder_1_out_3, not_1_out);
  and and_3 (and_3_out, decoder_1_out_4, Write);
  and and_4 (and_4_out, decoder_1_out_5, Write);
  and and_5 (and_5_out, decoder_1_out_5, not_1_out);
  and and_6 (and_6_out, decoder_1_out_6, Write);
  and and_7 (and_7_out, decoder_1_out_6, not_1_out);
  D_Latch d_latch_1 (.out_3(d_latch_1_out_3), .in_1(in_3), .in_2(and_1_out));
  D_Latch d_latch_2 (.out_3(d_latch_2_out_3), .in_1(in_3), .in_2(and_3_out));
  and and_8 (and_8_out, decoder_1_out_4, not_1_out);
  D_Latch d_latch_3 (.out_3(d_latch_3_out_3), .in_1(in_3), .in_2(and_4_out));
  D_Latch d_latch_4 (.out_3(d_latch_4_out_3), .in_1(in_3), .in_2(and_6_out));
  and and_9 (and_9_out, d_latch_1_out_3, and_2_out);
  and and_10 (and_10_out, d_latch_2_out_3, and_8_out);
  and and_11 (and_11_out, d_latch_3_out_3, and_5_out);
  and and_12 (and_12_out, d_latch_4_out_3, and_7_out);
  D_Latch d_latch_5 (.out_3(d_latch_5_out_3), .in_1(_3Bit_Data), .in_2(and_1_out));
  D_Latch d_latch_6 (.out_3(d_latch_6_out_3), .in_1(_3Bit_Data), .in_2(and_3_out));
  D_Latch d_latch_7 (.out_3(d_latch_7_out_3), .in_1(_3Bit_Data), .in_2(and_4_out));
  D_Latch d_latch_8 (.out_3(d_latch_8_out_3), .in_1(_3Bit_Data), .in_2(and_6_out));
  or or_1 (out_7, and_9_out, and_10_out, and_11_out, and_12_out);
  and and_13 (and_13_out, d_latch_5_out_3, and_2_out);
  and and_14 (and_14_out, d_latch_6_out_3, and_8_out);
  and and_15 (and_15_out, d_latch_7_out_3, and_5_out);
  and and_16 (and_16_out, d_latch_8_out_3, and_7_out);
  D_Latch d_latch_9 (.out_3(d_latch_9_out_3), .in_1(in_5), .in_2(and_1_out));
  D_Latch d_latch_10 (.out_3(d_latch_10_out_3), .in_1(in_5), .in_2(and_3_out));
  D_Latch d_latch_11 (.out_3(d_latch_11_out_3), .in_1(in_5), .in_2(and_4_out));
  D_Latch d_latch_12 (.out_3(d_latch_12_out_3), .in_1(in_5), .in_2(and_6_out));
  or or_2 (_3_Bit_Out, and_13_out, and_14_out, and_15_out, and_16_out);
  and and_17 (and_17_out, d_latch_9_out_3, and_2_out);
  and and_18 (and_18_out, d_latch_10_out_3, and_8_out);
  and and_19 (and_19_out, d_latch_11_out_3, and_5_out);
  and and_20 (and_20_out, d_latch_12_out_3, and_7_out);
  or or_3 (out_9, and_17_out, and_18_out, and_19_out, and_20_out);

  // Notes on the sheet:
  //   Name: Jason Qiu
  //   Implement  3 Bit, 4 Word RAM
  //   Implement the WRITE operation
  //   If you need help, look at slides 9-16 in week9.pdf
  //   The 3 Bit Output should reflect the values stored in the word selected by the 2Bit Addr
  //   Pledge: I pledge my honor that I have abided by the Stevens Honor System.
endmodule

module Remainder (
  input  in_1,
  input  in_2,
  input  in_3,
  input  Numerator,
  input  in_5,
  output out_6,
  output out_7,
  output out_8
);

  wire and_1_out, and_2_out, and_3_out, and_4_out, and_5_out, and_6_out, decoder_1_out_4, decoder_1_out_5,
       decoder_1_out_6, not_1_out, not_2_out, or_1_out, or_2_out, xor_1_out, xor_2_out;

  Decoder decoder_1 (
    .out_6(decoder_1_out_6), .out_3(out_6), .out_5(decoder_1_out_5), .out_4(decoder_1_out_4), .in_2(in_2),
    .in_1(in_1));
  and and_1 (and_1_out, in_3, Numerator, in_5);
  and and_2 (and_2_out, in_3, not_1_out, in_5);
  not not_1 (not_1_out, Numerator);
  ExactlyOne xor_1 (.out(xor_1_out), .in0(in_3), .in1(Numerator), .in2(in_5));
  and and_3 (and_3_out, xor_1_out, Numerator);
  ExactlyOne xor_2 (.out(xor_2_out), .in0(in_3), .in1(Numerator), .in2(in_5));
  and and_4 (and_4_out, xor_2_out, not_2_out);
  not not_2 (not_2_out, Numerator);
  and and_5 (and_5_out, in_5, decoder_1_out_5);
  and and_6 (and_6_out, decoder_1_out_6, or_1_out);
  or or_1 (or_1_out, and_1_out, and_4_out);
  or or_2 (or_2_out, and_2_out, and_3_out);
  or or_3 (out_8, and_5_out, and_6_out);
  and and_7 (out_7, or_2_out, decoder_1_out_6);

  // Notes on the sheet:
  //   Divisor
  //   (Hint: You may want to write a truth table first)
  //   Part 2: Create a circuit to calculate remainders, given a 3-bit numerator and 2-bit divisor.
  //   Discard 1; remainder is always 0 regardless.
  //   Error bit (Set when division isn't possible)
  //   Remainder
endmodule
