// Logisim project lab8.circ as structural Verilog: 2 circuits, main circuit ParityGenerator
module XOR (
  input  X,
  input  Y,
  output XOR
);

  wire and_1_out, and_2_out, not_1_out, not_2_out;

  not not_1 (not_1_out, X);
  not not_2 (not_2_out, Y);
  and and_1 (and_1_out, not_1_out, Y);
  and and_2 (and_2_out, X, not_2_out);
  or or_1 (XOR, and_1_out, and_2_out);

  // Notes on the sheet:
  //   Use minterm expansion to create an XOR gate using AND + OR gates
endmodule

module ParityGenerator (
  input  X,
  input  Y,
  input  Z,
  input  X_2,
  input  Y_2,
  input  Z_2,
  output Parity,
  output Parity_2
);

  wire and_1_out, and_2_out, and_3_out, and_4_out, not_1_out, not_2_out, not_3_out, not_4_out, or_1_out,
       xor_1_xor;

  not not_1 (not_1_out, X);
  not not_2 (not_2_out, Y);
  XOR xor_1 (.X(X_2), .XOR(xor_1_xor), .Y(Y_2));
  and and_1 (and_1_out, not_1_out, Y);
  not not_3 (not_3_out, or_1_out);
  not not_4 (not_4_out, Z);
  and and_2 (and_2_out, not_3_out, Z);
  XOR xor_2 (.X(xor_1_xor), .XOR(Parity_2), .Y(Z_2));
  and and_3 (and_3_out, X, not_2_out);
  and and_4 (and_4_out, or_1_out, not_4_out);
  or or_1 (or_1_out, and_1_out, and_3_out);
  or or_2 (Parity, and_2_out, and_4_out);

  // Notes on the sheet:
  //   Input Bits
  //   Write your parity circuit here
  //   the output = 1 if an odd number of inputs (1 or 3) are 1, otherwise 0
  //   ONLY use: NOT, AND, OR, and any custom functions you write (included in the .circ submission)
  //   WRITE YOUR NAME AND PLEDGE SOMEWHERE IN THIS CIRCUIT
  //   I pledge my honor that I have abided by the Stevens Honor System. - Jason Qiu
  //   The following two circuits are functionally equivalent; one is simplified with the XOR circuit.
endmodule
